# Fritzing sketch Lesson02_Button (saved by Fritzing 0.9.2b)
circuit board: 8.46667cm x 5.64444cm
breadboards: 1

parts:
  LED1 = LED - 5mm [color="Blue (505nm)" package="5 mm [THT]"]
  Raspberry_Pi1 = Raspberry Pi 2
  R2 = Resistor [tolerance=±5% resistance=10k package=THT]
  R1 = Resistor [tolerance=±5% resistance=220 package=THT]
  S1 = Momentary Switch [package=ksa_sealed_tac_switch]
  R3 = Resistor [tolerance=±5% resistance=1k package=THT]

nets:
  N1: LED1.cathode, R1.Pin_1
  N2: LED1.anode, Raspberry_Pi1.GPIO25
  3V3: Raspberry_Pi1.3v3, Raspberry_Pi1.3V3, S1.4
  N3: Raspberry_Pi1.GND, R2.Pin_1, R1.Pin_0
  N4: Raspberry_Pi1.GPIO24, R3.Pin_0
  N5: R2.Pin_0, S1.2
  N6: S1.1, R3.Pin_1
