# Fritzing sketch LessonXX_LCD (saved by Fritzing 0.9.2b)
circuit board: 8.46667cm x 5.64444cm
breadboards: 1

parts:
  part = Raspberry Pi 2
  LCD = LCD screen
  POT = Breadboard Trimpot

nets:
  GND: part.GND, LCD.VSS, LCD.R/W, LCD.DB0, LCD.DB1, LCD.DB2, LCD.DB3, LCD.LED-, POT.PIN1
  N1: part.GPIO25, LCD.RS
  N2: part.GPIO24, LCD.E
  N3: part.GPIO23, LCD.DB4
  N4: part.GPIO18, LCD.DB5
  N5: part.GPIO15, LCD.DB6
  N6: part.GPIO14, LCD.DB7
  5V: part.5V, LCD.VDD, LCD.LED+, POT.PIN3
  N7: LCD.V0, POT.PIN2
